# Fritzing sketch wiring (saved by Fritzing 0.9.2b)

parts:
  ARDUINO = Arduino Pro Mini v13
  MPU6050 = IMU Digital Combo Board 6DOF
  BMP280 = Barometric Pressure Sensor - BMP085 Breakout
  part = ESP8266 WiFi Module [part_number=ESP8266]
  U1 = LIPO-110mAh [package=lipo-110]  # not connected
  PULSE_SENSOR = RMCM01 [package=rmcm01]
  Part1 = Lilypad Battery Connect  # not connected
  EMERGENCY_BUTTON = Momentary Switch [package=ksa_sealed_tac_switch]
  CONFIGURATION_BUTTON = Momentary Switch [package=ksa_sealed_tac_switch]
  R1 = Resistor [tolerance=±5% resistance=10k package="1206 [SMD]"]
  R2 = Resistor [tolerance=±5% resistance=10k package="1206 [SMD]"]

nets:
  GND: ARDUINO.GND, ARDUINO.D2, MPU6050.INT0, part.GND
  N1: ARDUINO.VCC, part.CH_PD
  N2: ARDUINO.A0, PULSE_SENSOR.LX2
  N3: ARDUINO.D9_PWM, EMERGENCY_BUTTON.4
  N4: ARDUINO.D8, CONFIGURATION_BUTTON.4
  N5: ARDUINO.RESET, part.GPIO_2
  N6: ARDUINO.D1/RX, part.TXD
  N7: ARDUINO.D0/TX, part.RXD
  N8: BMP280.GND, EMERGENCY_BUTTON.1
  N9: EMERGENCY_BUTTON.3, R1.Pin_1
  N10: CONFIGURATION_BUTTON.3, R2.Pin_1

notes:
  RED - vcc
  BLACK - gnd
  GREEN - sda
  YELLOW - scl
  PURPLE - sd0
  PINK - cs

custom parts:
  ESP8266 WiFi Module: Generic WiFi Module based on the ESP8266 with onboard PCB antenna and UART communications
